// Logisim project ALU2.circ as structural Verilog
module ALU (
  input  [15:0] in_1,
  input  [15:0] in_2,
  input  [1:0] in_3,
  output out_4,
  output [15:0] out_5
);

  wire [15:0] and_1_out, multiplier_1_out, nor_1_out, shifter_1_out, subtractor_1_out;

  Shifter #(.width(16)) shifter_1 (.in(in_2), .\dist (in_1[3:0]), .out(shifter_1_out));
  assign and_1_out = in_1 & in_2;  // AND_Gate and_1, 16 bits wide
  assign nor_1_out = ~(in_1 | in_2);  // NOR_Gate nor_1, 16 bits wide
  Subtractor #(.width(16)) subtractor_1 (.a(in_1), .b(in_2), .out(subtractor_1_out));  // open: bin, bout
  Multiplier #(.width(16)) multiplier_1 (.a(in_1), .b(in_2), .out(multiplier_1_out));  // open: cin, cout
  Multiplexer #(.select(2), .width(16), .enable("false")) multiplexer_1 (
    .in0(and_1_out), .in1(nor_1_out), .in2(subtractor_1_out), .in3(multiplier_1_out),
    .out({out_4, out_5[14:0]}), .sel(in_3));

  assign out_5[15] = out_4;
endmodule

module CPU (
);

  wire controlunit_1_alusrc, controlunit_1_jump, controlunit_1_ra, controlunit_1_regdst,
       controlunit_1_regwrite, controlunit_1_slt;
  wire [1:0] controlunit_1_alucnt;
  wire [3:0] multiplexer_1_out, multiplexer_2_out, undriven_2, undriven_3;
  wire [7:0] undriven_4;
  wire [11:0] undriven;
  wire [15:0] adder_1_out, alu_1_out_5, bit_extender_1_out, bit_extender_2_out, concat_1_result,
       multiplexer_3_out, multiplexer_4_out, multiplexer_5_out, multiplexer_6_out, PC_q,
       registerfile_1_data1, registerfile_1_data2, rom_1_data;

  Register #(.width(16)) PC (.D(multiplexer_3_out), .Q(PC_q));  // open: en, clk, clr
  Adder #(.width(16)) adder_1 (.a(16'h2), .b(PC_q), .out(adder_1_out));  // open: cin, cout
  ROM #(.addrWidth(16), .dataWidth(16)) rom_1 (.addr(PC_q), .data(rom_1_data));  // open: sel
  Concat concat_1 (.in_1(undriven), .in_2(adder_1_out), .result(concat_1_result));
  Multiplexer #(.width(4)) multiplexer_1 (
    .in0(rom_1_data[11:8]), .in1(rom_1_data[7:4]), .out(multiplexer_1_out), .en(controlunit_1_regdst));  // open: sel
  Multiplexer #(.width(4)) multiplexer_2 (
    .in0(multiplexer_1_out), .in1(undriven_3), .out(multiplexer_2_out), .en(controlunit_1_ra));  // open: sel
  assign bit_extender_1_out = {{12{1'b0}}, undriven_2};  // Bit_Extender bit_extender_1
  Multiplexer #(.width(16)) multiplexer_3 (
    .in0(concat_1_result), .in1(adder_1_out), .out(multiplexer_3_out), .en(controlunit_1_jump));  // open: sel
  ControlUnit controlunit_1 (
    .in_1(rom_1_data[15:12]), .slt(controlunit_1_slt), .ALUsrc(controlunit_1_alusrc),
    .REGwrite(controlunit_1_regwrite), .jump(controlunit_1_jump), .regDst(controlunit_1_regdst),
    .ra(controlunit_1_ra), .ALUcnt(controlunit_1_alucnt));
  RegisterFile registerfile_1 (
    .Read_Register1(rom_1_data[3:0]), .Read_Register2(rom_1_data[7:4]), .writeData(multiplexer_6_out),
    .Data1(registerfile_1_data1), .Data2(registerfile_1_data2), .REGwrite(controlunit_1_regwrite),
    .write_register(multiplexer_2_out));  // open: clock
  Multiplexer #(.width(16)) multiplexer_4 (
    .in0(registerfile_1_data1), .in1(bit_extender_1_out), .out(multiplexer_4_out), .en(controlunit_1_alusrc));  // open: sel
  ALU alu_1 (.in_1(multiplexer_4_out), .in_2(registerfile_1_data2), .out_5(alu_1_out_5));  // open: in_3, out_4
  assign bit_extender_2_out = {{8{1'b0}}, undriven_4};  // Bit_Extender bit_extender_2
  Multiplexer #(.width(16)) multiplexer_5 (
    .in0(bit_extender_2_out), .in1(alu_1_out_5), .out(multiplexer_5_out), .en(controlunit_1_slt));  // open: sel
  Multiplexer #(.width(16)) multiplexer_6 (
    .in0(adder_1_out), .in1(multiplexer_5_out), .out(multiplexer_6_out), .en(controlunit_1_ra));  // open: sel

  // Notes on the sheet:
  //   pc+2
  //   contents of rom_1 (hex, n*v repeats v):
  //   410a
  //   R15
  //   16 bits
  //   less
endmodule

module ControlUnit (
  input  [3:0] in_1,
  output slt,
  output ALUsrc,
  output REGwrite,
  output jump,
  output regDst,
  output ra,
  output [1:0] ALUcnt
);

  wire and_out, andi_out, mul_out, nor_out, sll_out, slt_out, slti_out;

  and \nor  (nor_out, ~in_1[3], ~in_1[2], ~in_1[1], ~in_1[0]);  // AND_Gate
  and u_slt (slt_out, ~in_1[3], in_1[2], ~in_1[1], in_1[0]);  // AND_Gate
  and sll (sll_out, ~in_1[3], ~in_1[2], ~in_1[1], in_1[0]);  // AND_Gate
  and slti (slti_out, ~in_1[3], ~in_1[2], in_1[1], ~in_1[0]);  // AND_Gate
  and andi (andi_out, ~in_1[3], in_1[2], ~in_1[1], ~in_1[0]);  // AND_Gate
  and \and  (and_out, ~in_1[3], in_1[2], in_1[1], in_1[0]);  // AND_Gate
  and mul (mul_out, in_1[3], in_1[2], in_1[1], in_1[0]);
  and jal (jump, in_1[3], ~in_1[2], in_1[1], in_1[0]);  // AND_Gate
  or or_1 (ALUcnt[1], mul_out, slt_out, slti_out);
  or or_2 (ALUcnt[0], mul_out, nor_out);
  or or_3 (slt, slt_out, slti_out);
  or or_4 (ALUsrc, andi_out, slti_out);
  or or_5 (REGwrite, jump, mul_out, andi_out, and_out, slti_out, sll_out, slt_out, nor_out);
  or or_6 (regDst, andi_out, slti_out);

  assign ra = jump;
endmodule

module RegisterFile (
  input  REGwrite,
  input  [3:0] write_register,
  input  [3:0] Read_Register1,
  input  [3:0] Read_Register2,
  input  [15:0] writeData,
  input  clock,
  output [15:0] Data1,
  output [15:0] Data2
);

  wire and_1_out, and_2_out, and_3_out, and_4_out, and_5_out, and_6_out, and_7_out, and_8_out, and_9_out,
       and_10_out, and_11_out, and_12_out, and_13_out, and_14_out, and_15_out, and_16_out, decoder_1_out0,
       decoder_1_out1, decoder_1_out2, decoder_1_out3, decoder_1_out4, decoder_1_out5, decoder_1_out6,
       decoder_1_out7, decoder_1_out8, decoder_1_out9, decoder_1_out10, decoder_1_out11, decoder_1_out12,
       decoder_1_out13, decoder_1_out14, decoder_1_out15;
  wire [15:0] register_1_q, register_2_q, register_3_q, register_4_q, register_5_q, register_6_q,
       register_7_q, register_8_q, register_9_q, register_10_q, register_12_q, register_13_q, register_14_q,
       register_15_q, register_16_q;

  Decoder #(.select(4), .enable("false")) decoder_1 (
    .out0(decoder_1_out0), .out1(decoder_1_out1), .out2(decoder_1_out2), .out3(decoder_1_out3),
    .out4(decoder_1_out4), .out5(decoder_1_out5), .out6(decoder_1_out6), .out7(decoder_1_out7),
    .out8(decoder_1_out8), .out9(decoder_1_out9), .out10(decoder_1_out10), .out11(decoder_1_out11),
    .out12(decoder_1_out12), .out13(decoder_1_out13), .out14(decoder_1_out14), .out15(decoder_1_out15),
    .sel(write_register));
  and and_1 (and_1_out, decoder_1_out0, REGwrite);
  and and_2 (and_2_out, decoder_1_out1, REGwrite);
  and and_3 (and_3_out, decoder_1_out2, REGwrite);
  and and_4 (and_4_out, decoder_1_out3, REGwrite);
  and and_5 (and_5_out, decoder_1_out4, REGwrite);
  and and_6 (and_6_out, decoder_1_out5, REGwrite);
  and and_7 (and_7_out, decoder_1_out6, REGwrite);
  and and_8 (and_8_out, decoder_1_out7, REGwrite);
  Register #(.width(16)) register_1 (.D(writeData), .en(and_1_out), .Q(register_1_q), .clk(clock));  // open: clr
  Register #(.width(16)) register_2 (.en(and_2_out), .Q(register_2_q), .clk(clock));  // open: D, clr
  Register #(.width(16)) register_3 (.en(and_3_out), .Q(register_3_q), .clk(clock));  // open: D, clr
  Register #(.width(16)) register_4 (.en(and_4_out), .Q(register_4_q), .clk(clock));  // open: D, clr
  Register #(.width(16)) register_5 (.en(and_5_out), .Q(register_5_q), .clk(clock));  // open: D, clr
  Register #(.width(16)) register_6 (.en(and_6_out), .Q(register_6_q), .clk(clock));  // open: D, clr
  Register #(.width(16)) register_7 (.en(and_7_out), .Q(register_7_q), .clk(clock));  // open: D, clr
  Register #(.width(16)) register_8 (.en(and_8_out), .Q(register_8_q), .clk(clock));  // open: D, clr
  and and_9 (and_9_out, decoder_1_out8, REGwrite);
  and and_10 (and_10_out, decoder_1_out9, REGwrite);
  and and_11 (and_11_out, decoder_1_out10, REGwrite);
  and and_12 (and_12_out, decoder_1_out11, REGwrite);
  and and_13 (and_13_out, decoder_1_out12, REGwrite);
  and and_14 (and_14_out, decoder_1_out13, REGwrite);
  and and_15 (and_15_out, decoder_1_out14, REGwrite);
  and and_16 (and_16_out, decoder_1_out15, REGwrite);
  Register #(.width(16)) register_9 (.D(writeData), .en(and_9_out), .Q(register_9_q), .clk(clock));  // open: clr
  Register #(.width(16)) register_10 (.D(writeData), .en(and_10_out), .Q(register_10_q), .clk(clock));  // open: clr
  Register #(.width(16)) register_11 (.D(writeData), .en(and_11_out), .Q(register_10_q), .clk(clock));  // open: clr
  Register #(.width(16)) register_12 (.D(writeData), .en(and_12_out), .Q(register_12_q), .clk(clock));  // open: clr
  Register #(.width(16)) register_13 (.D(writeData), .en(and_13_out), .Q(register_13_q), .clk(clock));  // open: clr
  Register #(.width(16)) register_14 (.D(writeData), .en(and_14_out), .Q(register_14_q), .clk(clock));  // open: clr
  Register #(.width(16)) register_15 (.D(writeData), .en(and_15_out), .Q(register_15_q), .clk(clock));  // open: clr
  Register #(.width(16)) register_16 (.D(writeData), .en(and_16_out), .Q(register_16_q), .clk(clock));  // open: clr
  Multiplexer #(.select(4), .width(16)) multiplexer_1 (
    .in0(register_1_q), .in1(register_2_q), .in2(register_3_q), .in3(register_4_q), .in4(register_5_q),
    .in5(register_6_q), .in6(register_7_q), .in7(register_8_q), .in8(register_9_q), .in9(register_10_q),
    .in10(register_10_q), .in11(register_12_q), .in12(register_13_q), .in13(register_14_q),
    .in14(register_15_q), .in15(register_16_q), .out(Data1), .sel(Read_Register1));  // open: en
  Multiplexer #(.select(4), .width(16)) multiplexer_2 (
    .in0(register_1_q), .in1(register_2_q), .in2(register_3_q), .in3(register_4_q), .in4(register_5_q),
    .in5(register_6_q), .in6(register_7_q), .in7(register_8_q), .in8(register_9_q), .in9(register_10_q),
    .in10(register_10_q), .in11(register_12_q), .in12(register_13_q), .in13(register_14_q),
    .in14(register_15_q), .in15(register_16_q), .out(Data2), .sel(Read_Register2));  // open: en
endmodule

module Concat (
  input  [11:0] in_1,
  input  [15:0] in_2,
  output [15:0] result
);

  wire [13:0] bit_extender_1_out;

  assign bit_extender_1_out = {{2{1'b0}}, in_1};  // Bit_Extender bit_extender_1
  Shifter #(.width(14)) shifter_1 (.in(bit_extender_1_out), .\dist (4'b0010), .out(result[13:0]));

  assign result[15:14] = in_2[15:14];
endmodule
